# Fritzing sketch fritzing schematic (saved by Fritzing 0.9.3b)

parts:
  Part1 = Arduino Uno (Rev3) - ICSP
  Part2 = BH1750
  Squix4 = OLED 0.96" 128x64 I2C SSD1306
  R1 = Rotary Potentiometer (Small) [maximum_resistance=100kΩ package=THT]
  S1 = Pushbutton [package="[THT]"]

nets:
  N1: Part1.A0, R1.wiper
  N2: Part1.A4/SDA, Part2.SDA, Squix4.SCA
  N3: Part1.A5/SCL, Part2.SCL, Squix4.SCL
  N4: Part1.D10_PWM/SS, Squix4.VCC
  N5: Part1.D3_PWM, S1.Pin_1, S1.Pin_2
  5V: Part1.5V, Part2.VCC, R1.leg1
  GND: Part1.GND, Part2.GND, Squix4.GND, R1.leg2, S1.Pin_4

custom parts:
  BH1750: Light Sensor
